# Fritzing sketch Esquema (saved by Fritzing 0.9.3b)
circuit board: 8.46667cm x 5.64444cm
breadboards: 1

parts:
  U1 = ESP8266 WiFi Module [part_number=ESP8266]
  U2 = NEO 6M GPS
  BATT1 = LiPoly Battery (1300mAh)
  S2 = Round Pushbutton
  R1 = Resistor [tolerance=±5% resistance=220 package="0805 [SMD]"]
  S3 = SPST Switch [package=switch-spst-smd-a]

nets:
  N1: U1.RXD, S2.leg0, R1.Pin_1
  VCC: U1.VCC, U2.VCC, BATT1.positive, S3.S
  N2: U1.GPIO_0, U2.TXD
  N3: U1.GPIO_2, U2.RXD
  GND: U1.GND, U2.GND, BATT1.negative, R1.Pin_0
  N4: S2.leg1, S3.P

custom parts:
  ESP8266 WiFi Module: Generic WiFi Module based on the ESP8266 with onboard PCB antenna and UART communications
  NEO 6M GPS: uSD module
  LiPoly Battery (1300mAh): Lithium Ion Polymer Battery (1300mAh)
